# Fritzing sketch Untitled Sketch (saved by Fritzing 0.9.3b)
breadboards: 1

parts:
  U1 = NodeMCU V1.0
  S1 = Momentary Switch [package=ksa_sealed_tac_switch]
  S2 = Momentary Switch [package=ksa_sealed_tac_switch]
  S3 = Momentary Switch [package=ksa_sealed_tac_switch]
  S4 = Momentary Switch [package=ksa_sealed_tac_switch]
  Display1 = LCD screen 16x2 IIC [part_number=101290]
  Pololu_A1 = Pololu A4988 [package=SO16]
  U2 = LM2596 step down module
  M1 = Stepper Motor - Bipolar
  JACK1 = 2.1mm Barrel Jack with Terminal Block

nets:
  N1: U1.D0, S4.4
  N2: U1.D1, Display1.SDA
  N3: U1.D2, Display1.SCL
  N4: U1.D3, Pololu_A1.DIR
  N5: U1.D4, Pololu_A1.STEP
  N6: U1.GND, U1.D5, S1.4
  N7: U1.D6, S2.4
  N8: U1.D7, S3.4
  VCC: S1.1, S2.1, S3.1, S4.1, Display1.VCC, Pololu_A1.VDD, U2.OUT+
  GND: Display1.GND, Pololu_A1.GND, U2.IN-, U2.OUT-, JACK1.POS
  N9: Pololu_A1.1B, M1.D
  N10: Pololu_A1.1A, M1.B
  N11: Pololu_A1.2A, M1.C
  N12: Pololu_A1.2B, M1.A
  N13: Pololu_A1.VMOT, U2.IN+, JACK1.NEG

custom parts:
  NodeMCU V1.0: ESP8266 based NodeMCU
  LCD screen 16x2 IIC: LCD screen with HD44780 controller enables showing text, symbols, value or anything else that comes from Croduino/Arduino. It is capable of showing 16 symbols in two lines and therefore can be used in many projects that need to send clearly visible and legible output information.. • Color of symbols: White • Backlight: Blue • Dimensions: 80 x 36 x 12 mm • Screen dimensions: 64.5 x 16 mm •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
  LM2596 step down module: LM2596 DC-DC step down power supply module 3 A.
